// Digital circuit decreasing_mem.dig as structural Verilog
module decreasing_mem (
  input  clock,
  input  [31:0] A,
  output [31:0] \output 
);

  wire comp_eq, comp_gt, comp_lt;
  wire [31:0] mem_nq, multiplexer_1_out;

  Comparator #(.Bits(32)) comp (.a(A), .b(\output ), .gt(comp_gt), .eq(comp_eq), .lt(comp_lt));
  Multiplexer #(.Bits(32)) multiplexer_1 (.sel(comp_lt), .in_0(\output ), .in_1(A), .out(multiplexer_1_out));
  D_FF #(.Bits(32), .Default(2147483647)) mem (.D(multiplexer_1_out), .C(clock), .Q(\output ), .nQ(mem_nq));

  // Notes on the sheet:
  //   clock: Hz: 80000
  //   A: default 2147483647
endmodule
