// Digital circuit node_module.dig as structural Verilog
module node_module (
  input  start,
  input  clock,
  input  clr,
  output [31:0] own
);

  wires_in #(.generic("in_nodes := args.neighbourhood_size;")) wires_in_1 ();
  decreasing_mem decreasing_mem_1 (.clock(clock), .set(clr), .clr(start), .\output (own));  // open: A
  wires_out #(.generic("out_nodes := args.neighbourhood_size; weights := args.edge_weights;")) wires_out_1 (.in(own));

  // Notes on the sheet:
  //   clock: Hz: 50000
endmodule

/* Test case:
clock clr start I0 I1 I2 I3 own O0 O1 O2 O3

############################ Vertex 0 to every other Vertex 

0 1 0 10 10 10 10 2147483647 2147483648 2147483649 2147483651 2147483655 # reset line

C 0 0 10 10 10 10 10 11 12 14 18

C 0 0 10 5 10 10 5 6 7 9 13

C 1 0 10 5 10 10 2147483647 2147483648 2147483649 2147483651 2147483655

C 0 0 50 50 50 50 50 51 52 54 58

C 0 0 50 3 50 50 3 4 5 7 11

C 0 1 50 3 50 50 0 1 2 4 8

C 1 0 50 3 50 50 2147483647 2147483648 2147483649 2147483651 2147483655

C 0 0 50 3 50 50 3 4 5 7 11
*/

/* Code that sets the parameters or builds the circuit:
neighbourhood_size:=4;
edge_weights:=[4,8,1,1,1,1];
*/

/* Code that sets the parameters or builds the circuit:
x_output_start := 33;
y_output_start := 8;
y_output_add:= 1;

x_input_start := 15;
y_input_start := 6;
y_input_add:= 1;

y_input_offset:=0;

for (i:=0;i<args.neighbourhood_size;i++){
    output:=addComponent("Out",x_output_start,y_output_start+i*y_output_add);
    output.Bits=32;
    output.Label="O"+i;
}

for (i:=0;i<args.neighbourhood_size;i++){
    if(args.neighbourhood_size%2=0)
    {
	if(i>=args.neighbourhood_size/2){
	   y_input_offset = 1;
	}
    }
    output:=addComponent("In",x_input_start,y_input_start+i*y_input_add + y_input_offset);
    output.Bits=32;
    output.Label="I"+i;
}

addWire(x_input_start+3,y_input_start + args.neighbourhood_size/2,23,8);
*/
