// Digital circuit decreasing_mem.dig as structural Verilog
module decreasing_mem (
  input  clk,
  input  [31:0] in,
  input  set,
  input  clr,
  input  [31:0] din,
  output [31:0] out,
  output [31:0] dout
);

  wire and_1_out, comp_eq, comp_gt, comp_lt, or_1_out, or_2_out;
  wire [31:0] data_nq, value_nq;

  Comparator #(.Bits(32)) comp (.a(in), .b(out), .gt(comp_gt), .eq(comp_eq), .lt(comp_lt));
  and and_1 (and_1_out, or_1_out, clk);
  or or_1 (or_1_out, comp_eq, comp_lt);
  or or_2 (or_2_out, set, clr);
  D_FF_AS #(.Bits(32), .Default(2000000)) value (.Set(set), .D(in), .C(and_1_out), .Clr(clr), .Q(out), .nQ(value_nq));
  D_FF_AS #(.Bits(32)) data (.Set(set), .D(din), .C(and_1_out), .Clr(or_2_out), .Q(dout), .nQ(data_nq));

  // Notes on the sheet:
  //   in: default 1
  //   din: default 1
endmodule

/* Test case:
clk clr set in out

############################

0 1 0 10 0

C 0 0 10 0

C 0 1 10 4294967295

C 0 0 10 10

C 0 0 50 10

C 0 1 50 4294967295

C 0 0 50 50

C 0 0 10 10
*/
