// Digital circuit example.dig as structural Verilog
module example (
  input  clk,
  input  [31:0] VT,
  input  [31:0] VS,
  input  clr,
  output [31:0] SP
);

  wire _0_p4, _0_p5, _0_p6, _0_p7, _0_p8, _1_p5, _1_p6, _1_p7, _1_p9, _1_p10, _2_p5, _2_p6, _2_p7, _2_p8,
       _2_p10, _2_p11, _2_p12, _3_p5, _3_p6, _3_p7, _3_p9, _3_p10, _4_p5, _4_p6, _4_p8, _5_p7, _5_p8, _5_p12,
       _6_p5, _6_p6, _6_p7, _6_p8, _6_p10, _7_p7, _7_p8, _7_p11, _8_p7, demultiplexer_1_out_0,
       demultiplexer_1_out_1, demultiplexer_1_out_2, demultiplexer_1_out_3, demultiplexer_1_out_4,
       demultiplexer_1_out_5, demultiplexer_1_out_6, demultiplexer_1_out_7, demultiplexer_1_out_8,
       demultiplexer_1_out_9, demultiplexer_1_out_10, demultiplexer_1_out_11, demultiplexer_1_out_12,
       demultiplexer_1_out_13, demultiplexer_1_out_14, demultiplexer_1_out_15;

  Demultiplexer #(.Selector_Bits(4)) demultiplexer_1 (
    .sel(VS[3:0]), .in(1'b1), .out_0(demultiplexer_1_out_0), .out_1(demultiplexer_1_out_1),
    .out_2(demultiplexer_1_out_2), .out_3(demultiplexer_1_out_3), .out_4(demultiplexer_1_out_4),
    .out_5(demultiplexer_1_out_5), .out_6(demultiplexer_1_out_6), .out_7(demultiplexer_1_out_7),
    .out_8(demultiplexer_1_out_8), .out_9(demultiplexer_1_out_9), .out_10(demultiplexer_1_out_10),
    .out_11(demultiplexer_1_out_11), .out_12(demultiplexer_1_out_12), .out_13(demultiplexer_1_out_13),
    .out_14(demultiplexer_1_out_14), .out_15(demultiplexer_1_out_15));
  // node_module #(.generic("edge_weights := [4,8]; neighbourhood_size := 2;")) _0: pin names not known; wires that end beside it: demultiplexer_1_out_0, clk, clr, _0_p4, _0_p5, _0_p6, _0_p7, _0_p8
  // node_module #(.generic("edge_weights := [4,8,11]; neighbourhood_size := 3;")) _1: pin names not known; wires that end beside it: demultiplexer_1_out_1, clk, clr, _0_p7, _1_p5, _1_p6, _1_p7, _0_p4, _1_p9, _1_p10
  // node_module #(.generic("edge_weights := [8,7,4,2]; neighbourhood_size := 4;")) _2: pin names not known; wires that end beside it: demultiplexer_1_out_2, clk, clr, _1_p9, _2_p5, _2_p6, _2_p7, _2_p8, _1_p5, _2_p10, _2_p11, _2_p12
  // node_module #(.generic("edge_weights := [7, 9, 14]; neighbourhood_size := 3;")) _3: pin names not known; wires that end beside it: demultiplexer_1_out_3, clk, clr, _2_p10, _3_p5, _3_p6, _3_p7, _2_p5, _3_p9, _3_p10
  // node_module #(.generic("edge_weights := [9,10]; neighbourhood_size := 2;")) _4: pin names not known; wires that end beside it: demultiplexer_1_out_4, clk, clr, _3_p9, _4_p5, _4_p6, _3_p5, _4_p8
  // node_module #(.generic("edge_weights := [4, 14, 10, 2]; neighbourhood_size := 4;")) _5: pin names not known; wires that end beside it: demultiplexer_1_out_5, clk, clr, _2_p11, _3_p10, _4_p8, _5_p7, _5_p8, _2_p6, _3_p6, _4_p5, _5_p12
  // node_module #(.generic("edge_weights := [ 6, 2, 1]; neighbourhood_size := 3;")) _6: pin names not known; wires that end beside it: demultiplexer_1_out_6, clk, clr, _5_p12, _6_p5, _6_p6, _6_p7, _6_p8, _5_p7, _6_p10
  // node_module #(.generic("edge_weights := [8,11, 7,1]; neighbourhood_size := 4;")) _7: pin names not known; wires that end beside it: demultiplexer_1_out_7, clk, clr, _0_p8, _1_p10, _6_p10, _7_p7, _7_p8, _0_p5, _1_p6, _7_p11, _6_p5
  // node_module #(.generic("edge_weights := [2, 6, 7]; neighbourhood_size := 3;")) _8: pin names not known; wires that end beside it: demultiplexer_1_out_8, clk, clr, _2_p12, _6_p8, _7_p11, _8_p7, _2_p7, _6_p6, _7_p7
  // extract_path #(.generic("number_of_inputs := 9;")) extract_path_1: pin names not known; wires that end beside it: VT, clk, clr, _0_p6, _1_p7, _2_p8, _3_p7, _4_p6, _5_p8, _6_p7, _7_p8, _8_p7, SP
endmodule

/* Test case:
clock clr VS VT  SP

############################ Vertex 0 to every other Vertex 
loop(s,9)
  loop(t,9)
    C 1 (s) (t) 0 # reset line

    loop(a,8)
      C 0 (s) (t) 0
    end loop

    C 0 (s) (t) X
  end loop
end loop
*/
